// Logisim project RAMfinalver45.circ as structural Verilog: 8 circuits, main circuit main
module main (
  input  addr_input,
  input  in_2,
  input  mode,
  input  in_4,
  input  in_5,
  input  data_input,
  input  in_7,
  output out_8,
  output out_9,
  output out_10,
  output out_11
);

  wire A00_out, A01_out, A10_out, A11_out, and_1_out, and_2_out, and_3_out, and_4_out, clock_1_out,
       clock_2_out, clock_3_out, clock_4_out, clock_5_out, clock_6_out, clock_7_out, d_ff_1_q, d_ff_2_q,
       d_ff_3_q, d_ff_4_q, d_ff_5_q, d_ff_6_q, mem_cell0_1_output, mem_cell0_2_output, mem_cell0_3_output,
       mem_cell0_4_output, mem_cell0_5_output, mem_cell0_6_output, mem_cell0_7_output, mem_cell0_8_output,
       mem_cell0_9_output, mem_cell0_10_output, mem_cell0_11_output, mem_cell0_12_output,
       mem_cell0_13_output, mem_cell0_14_output, mem_cell0_15_output, mem_cell0_16_output, not_1_out,
       not_2_out, not_3_out, not_4_out, not_5_out, not_6_out, or_1_out, or_2_out, or_3_out, or_4_out,
       rw_register0_1_output;

  Clock clock_1 (.out(clock_1_out));
  not not_1 (not_1_out, d_ff_1_q);
  D_Flip_Flop d_ff_1 (.D(addr_input), .clk(clock_1_out), .Q(d_ff_1_q));  // open: Qn, preset, reset
  D_Flip_Flop d_ff_2 (.D(in_2), .clk(clock_1_out), .Q(d_ff_2_q));  // open: Qn, preset, reset
  and A00 (A00_out, not_1_out, not_2_out);
  not not_2 (not_2_out, d_ff_2_q);
  Clock clock_2 (.out(clock_2_out));
  mem_cell0 mem_cell0_1 (
    .\input (d_ff_3_q), .mode(rw_register0_1_output), .select(A00_out), .\output (mem_cell0_1_output));
  mem_cell0 mem_cell0_2 (
    .\input (d_ff_4_q), .mode(rw_register0_1_output), .select(A00_out), .\output (mem_cell0_2_output));
  mem_cell0 mem_cell0_3 (
    .\input (d_ff_5_q), .mode(rw_register0_1_output), .select(A00_out), .\output (mem_cell0_3_output));
  mem_cell0 mem_cell0_4 (
    .\input (d_ff_6_q), .mode(rw_register0_1_output), .select(A00_out), .\output (mem_cell0_4_output));
  and A01 (A01_out, not_1_out, d_ff_2_q);
  and and_1 (and_1_out, rw_register0_1_output, in_4);
  and and_2 (and_2_out, in_5, rw_register0_1_output);
  and and_3 (and_3_out, rw_register0_1_output, data_input);
  and and_4 (and_4_out, in_7, rw_register0_1_output);
  Clock clock_3 (.out(clock_3_out));
  Clock clock_4 (.out(clock_4_out));
  D_Flip_Flop d_ff_3 (.D(and_1_out), .clk(clock_5_out), .Q(d_ff_3_q));  // open: Qn, preset, reset
  Clock clock_5 (.out(clock_5_out));
  D_Flip_Flop d_ff_4 (.D(and_2_out), .clk(clock_5_out), .Q(d_ff_4_q));  // open: Qn, preset, reset
  D_Flip_Flop d_ff_5 (.D(and_3_out), .clk(clock_5_out), .Q(d_ff_5_q));  // open: Qn, preset, reset
  D_Flip_Flop d_ff_6 (.D(and_4_out), .clk(clock_5_out), .Q(d_ff_6_q));  // open: Qn, preset, reset
  mem_cell0 mem_cell0_5 (
    .\input (d_ff_3_q), .mode(rw_register0_1_output), .select(A01_out), .\output (mem_cell0_5_output));
  mem_cell0 mem_cell0_6 (
    .\input (d_ff_4_q), .mode(rw_register0_1_output), .select(A01_out), .\output (mem_cell0_6_output));
  mem_cell0 mem_cell0_7 (
    .\input (d_ff_5_q), .mode(rw_register0_1_output), .select(A01_out), .\output (mem_cell0_7_output));
  mem_cell0 mem_cell0_8 (
    .\input (d_ff_6_q), .mode(rw_register0_1_output), .select(A01_out), .\output (mem_cell0_8_output));
  RW_register0 rw_register0_1 (.\input (mode), .in_2(clock_4_out), .\output (rw_register0_1_output));
  and A10 (A10_out, d_ff_1_q, not_2_out);
  Clock clock_6 (.out(clock_6_out));
  mem_cell0 mem_cell0_9 (
    .\input (d_ff_3_q), .mode(rw_register0_1_output), .select(A10_out), .\output (mem_cell0_9_output));
  mem_cell0 mem_cell0_10 (
    .\input (d_ff_4_q), .mode(rw_register0_1_output), .select(A10_out), .\output (mem_cell0_10_output));
  mem_cell0 mem_cell0_11 (
    .\input (d_ff_5_q), .mode(rw_register0_1_output), .select(A10_out), .\output (mem_cell0_11_output));
  mem_cell0 mem_cell0_12 (
    .\input (d_ff_6_q), .mode(rw_register0_1_output), .select(A10_out), .\output (mem_cell0_12_output));
  and and_5 (out_8, or_1_out, not_3_out);
  not not_3 (not_3_out, rw_register0_1_output);
  and and_6 (out_9, or_2_out, not_4_out);
  not not_4 (not_4_out, rw_register0_1_output);
  and and_7 (out_10, or_3_out, not_5_out);
  not not_5 (not_5_out, rw_register0_1_output);
  and and_8 (out_11, or_4_out, not_6_out);
  not not_6 (not_6_out, rw_register0_1_output);
  and A11 (A11_out, d_ff_1_q, d_ff_2_q);
  Clock clock_7 (.out(clock_7_out));
  mem_cell0 mem_cell0_13 (
    .\input (d_ff_3_q), .mode(rw_register0_1_output), .select(A11_out), .\output (mem_cell0_13_output));
  mem_cell0 mem_cell0_14 (
    .\input (d_ff_4_q), .mode(rw_register0_1_output), .select(A11_out), .\output (mem_cell0_14_output));
  mem_cell0 mem_cell0_15 (
    .\input (d_ff_5_q), .mode(rw_register0_1_output), .select(A11_out), .\output (mem_cell0_15_output));
  mem_cell0 mem_cell0_16 (
    .\input (d_ff_6_q), .mode(rw_register0_1_output), .select(A11_out), .\output (mem_cell0_16_output));
  or or_1 (or_1_out, mem_cell0_1_output, mem_cell0_5_output, mem_cell0_9_output, mem_cell0_13_output);
  or or_2 (or_2_out, mem_cell0_2_output, mem_cell0_6_output, mem_cell0_10_output, mem_cell0_14_output);
  or or_3 (or_3_out, mem_cell0_3_output, mem_cell0_7_output, mem_cell0_11_output, mem_cell0_15_output);
  or or_4 (or_4_out, mem_cell0_4_output, mem_cell0_8_output, mem_cell0_12_output, mem_cell0_16_output);

  // Notes on the sheet:
  //   ADDRESS REGISTER
  //   data space
  //   adsress space
  //   RAM
  //   R/W REGISTER
  //   DATA REGISTER
  //   clk
  //   data output
endmodule

module mem_cell0 (
  input  \input ,
  input  mode,
  input  select,
  output \output 
);

  wire and_1_out, and_2_out, clock_1_out, not_1_out, not_2_out, s_r_ff_1_q;

  and and_1 (and_1_out, mode, select, not_1_out);
  not not_1 (not_1_out, \input );
  S_R_Flip_Flop s_r_ff_1 (.S(and_2_out), .R(and_1_out), .clk(clock_1_out), .Q(s_r_ff_1_q));  // open: reset, Qn, preset
  and and_2 (and_2_out, \input , mode, select);
  Clock clock_1 (.out(clock_1_out));
  not not_2 (not_2_out, mode);
  and and_3 (\output , s_r_ff_1_q, not_2_out, select);

  // Notes on the sheet:
  //   clk
endmodule

module RW_register0 (
  input  \input ,
  input  in_2,
  output \output 
);

  wire not_1_out;

  J_K_Flip_Flop j_k_ff_1 (.J(\input ), .K(not_1_out), .clk(in_2), .Q(\output ));  // open: Qn, preset, reset
  not not_1 (not_1_out, \input );
endmodule

module RAM_16bytes (
  input  address_input,
  input  in_2,
  input  in_3,
  input  in_4,
  input  in_5,
  input  in_6,
  input  in_7,
  input  in_8,
  input  mode_input,
  input  data_input,
  input  in_11,
  input  in_12,
  input  in_13,
  input  in_14,
  input  in_15,
  input  in_16,
  input  in_17,
  output out_18,
  output out_19,
  output out_20,
  output out_21,
  output out_22,
  output out_23,
  output out_24,
  output out_25
);

  wire A0000_out, A0001_out, A0010_out, A0011_out, A0100_out, A0101_out, A0110_out, A0111_out, A111_out,
       A1000_out, A1001_out, A1010_out, A1011_out, A1100_out, A1101_out, A1110_out, clock_1_out, clock_2_out,
       clock_3_out, clock_4_out, clock_5_out, clock_6_out, clock_7_out, clock_8_out, clock_9_out,
       clock_10_out, clock_11_out, clock_12_out, clock_13_out, clock_14_out, clock_15_out, clock_16_out,
       mem_cell0_1_output, mem_cell0_2_output, mem_cell0_3_output, mem_cell0_4_output, mem_cell0_5_output,
       mem_cell0_6_output, mem_cell0_7_output, mem_cell0_8_output, mem_cell0_9_output, mem_cell0_10_output,
       mem_cell0_11_output, mem_cell0_12_output, mem_cell0_13_output, mem_cell0_14_output,
       mem_cell0_15_output, mem_cell0_16_output, mem_cell0_17_output, mem_cell0_18_output,
       mem_cell0_19_output, mem_cell0_20_output, mem_cell0_21_output, mem_cell0_22_output,
       mem_cell0_23_output, mem_cell0_24_output, mem_cell0_25_output, mem_cell0_26_output,
       mem_cell0_27_output, mem_cell0_28_output, mem_cell0_29_output, mem_cell0_30_output,
       mem_cell0_31_output, mem_cell0_32_output, mem_cell0_33_output, mem_cell0_34_output,
       mem_cell0_35_output, mem_cell0_36_output, mem_cell0_37_output, mem_cell0_38_output,
       mem_cell0_39_output, mem_cell0_40_output, mem_cell0_41_output, mem_cell0_42_output,
       mem_cell0_43_output, mem_cell0_44_output, mem_cell0_45_output, mem_cell0_46_output,
       mem_cell0_47_output, mem_cell0_48_output, mem_cell0_49_output, mem_cell0_50_output,
       mem_cell0_51_output, mem_cell0_52_output, mem_cell0_53_output, mem_cell0_54_output,
       mem_cell0_55_output, mem_cell0_56_output, mem_cell0_57_output, mem_cell0_58_output,
       mem_cell0_59_output, mem_cell0_60_output, mem_cell0_61_output, mem_cell0_62_output,
       mem_cell0_63_output, mem_cell0_64_output, mem_cell0_65_output, mem_cell0_66_output,
       mem_cell0_67_output, mem_cell0_68_output, mem_cell0_69_output, mem_cell0_70_output,
       mem_cell0_71_output, mem_cell0_72_output, mem_cell0_73_output, mem_cell0_74_output,
       mem_cell0_75_output, mem_cell0_76_output, mem_cell0_77_output, mem_cell0_78_output,
       mem_cell0_79_output, mem_cell0_80_output, mem_cell0_81_output, mem_cell0_82_output,
       mem_cell0_83_output, mem_cell0_84_output, mem_cell0_85_output, mem_cell0_86_output,
       mem_cell0_87_output, mem_cell0_88_output, mem_cell0_89_output, mem_cell0_90_output,
       mem_cell0_91_output, mem_cell0_92_output, mem_cell0_93_output, mem_cell0_94_output,
       mem_cell0_95_output, mem_cell0_96_output, mem_cell0_97_output, mem_cell0_98_output,
       mem_cell0_99_output, mem_cell0_100_output, mem_cell0_101_output, mem_cell0_102_output,
       mem_cell0_103_output, mem_cell0_104_output, mem_cell0_105_output, mem_cell0_106_output,
       mem_cell0_107_output, mem_cell0_108_output, mem_cell0_109_output, mem_cell0_110_output,
       mem_cell0_111_output, mem_cell0_112_output, mem_cell0_113_output, mem_cell0_114_output,
       mem_cell0_115_output, mem_cell0_116_output, mem_cell0_117_output, mem_cell0_118_output,
       mem_cell0_119_output, mem_cell0_120_output, mem_cell0_121_output, mem_cell0_122_output,
       mem_cell0_123_output, mem_cell0_124_output, mem_cell0_125_output, mem_cell0_126_output,
       mem_cell0_127_output, mem_cell0_128_output, not_1_out, not_2_out, not_3_out, not_4_out, not_5_out,
       not_6_out, not_7_out, not_8_out, or_1_out, or_2_out, or_3_out, or_4_out, or_5_out, or_6_out, or_7_out,
       or_8_out, or_9_out, or_10_out, or_11_out, or_12_out, or_13_out, or_14_out, or_15_out, or_16_out,
       or_17_out, or_18_out, or_19_out, or_20_out, or_21_out, or_22_out, or_23_out, or_24_out, or_25_out,
       or_26_out, or_27_out, or_28_out, or_29_out, or_30_out, or_31_out, or_32_out;

  and A0000 (A0000_out, address_input, in_3, in_5, in_7);
  Clock clock_1 (.out(clock_1_out));
  mem_cell0 mem_cell0_1 (.\input (data_input), .mode(mode_input), .select(A0000_out), .\output (mem_cell0_1_output));
  mem_cell0 mem_cell0_2 (.\input (in_11), .mode(mode_input), .select(A0000_out), .\output (mem_cell0_2_output));
  mem_cell0 mem_cell0_3 (.\input (in_12), .mode(mode_input), .select(A0000_out), .\output (mem_cell0_3_output));
  mem_cell0 mem_cell0_4 (.\input (in_13), .mode(mode_input), .select(A0000_out), .\output (mem_cell0_4_output));
  mem_cell0 mem_cell0_5 (.\input (in_14), .mode(mode_input), .select(A0000_out), .\output (mem_cell0_5_output));
  mem_cell0 mem_cell0_6 (.\input (in_15), .mode(mode_input), .select(A0000_out), .\output (mem_cell0_6_output));
  mem_cell0 mem_cell0_7 (.\input (in_16), .mode(mode_input), .select(A0000_out), .\output (mem_cell0_7_output));
  mem_cell0 mem_cell0_8 (.\input (in_17), .mode(mode_input), .select(A0000_out), .\output (mem_cell0_8_output));
  and A0001 (A0001_out, address_input, in_3, in_5, in_8);
  Clock clock_2 (.out(clock_2_out));
  mem_cell0 mem_cell0_9 (.\input (data_input), .mode(mode_input), .select(A0001_out), .\output (mem_cell0_9_output));
  mem_cell0 mem_cell0_10 (.\input (in_11), .mode(mode_input), .select(A0001_out), .\output (mem_cell0_10_output));
  mem_cell0 mem_cell0_11 (.\input (in_12), .mode(mode_input), .select(A0001_out), .\output (mem_cell0_11_output));
  mem_cell0 mem_cell0_12 (.\input (in_13), .mode(mode_input), .select(A0001_out), .\output (mem_cell0_12_output));
  mem_cell0 mem_cell0_13 (.\input (in_14), .mode(mode_input), .select(A0001_out), .\output (mem_cell0_13_output));
  mem_cell0 mem_cell0_14 (.\input (in_15), .mode(mode_input), .select(A0001_out), .\output (mem_cell0_14_output));
  mem_cell0 mem_cell0_15 (.\input (in_16), .mode(mode_input), .select(A0001_out), .\output (mem_cell0_15_output));
  mem_cell0 mem_cell0_16 (.\input (in_17), .mode(mode_input), .select(A0001_out), .\output (mem_cell0_16_output));
  and A0010 (A0010_out, address_input, in_3, in_6, in_7);
  Clock clock_3 (.out(clock_3_out));
  mem_cell0 mem_cell0_17 (.\input (data_input), .mode(mode_input), .select(A0010_out), .\output (mem_cell0_17_output));
  mem_cell0 mem_cell0_18 (.\input (in_11), .mode(mode_input), .select(A0010_out), .\output (mem_cell0_18_output));
  mem_cell0 mem_cell0_19 (.\input (in_12), .mode(mode_input), .select(A0010_out), .\output (mem_cell0_19_output));
  mem_cell0 mem_cell0_20 (.\input (in_13), .mode(mode_input), .select(A0010_out), .\output (mem_cell0_20_output));
  mem_cell0 mem_cell0_21 (.\input (in_14), .mode(mode_input), .select(A0010_out), .\output (mem_cell0_21_output));
  mem_cell0 mem_cell0_22 (.\input (in_15), .mode(mode_input), .select(A0010_out), .\output (mem_cell0_22_output));
  mem_cell0 mem_cell0_23 (.\input (in_16), .mode(mode_input), .select(A0010_out), .\output (mem_cell0_23_output));
  mem_cell0 mem_cell0_24 (.\input (in_17), .mode(mode_input), .select(A0010_out), .\output (mem_cell0_24_output));
  and and_1 (out_18, or_25_out, not_1_out);
  not not_1 (not_1_out, mode_input);
  and and_2 (out_19, or_26_out, not_2_out);
  not not_2 (not_2_out, mode_input);
  and and_3 (out_20, or_27_out, not_3_out);
  not not_3 (not_3_out, mode_input);
  and and_4 (out_21, or_28_out, not_4_out);
  not not_4 (not_4_out, mode_input);
  and and_5 (out_22, or_29_out, not_5_out);
  not not_5 (not_5_out, mode_input);
  and and_6 (out_23, or_30_out, not_6_out);
  not not_6 (not_6_out, mode_input);
  and and_7 (out_24, or_31_out, not_7_out);
  not not_7 (not_7_out, mode_input);
  and and_8 (out_25, or_32_out, not_8_out);
  not not_8 (not_8_out, mode_input);
  and A0011 (A0011_out, address_input, in_3, in_6, in_8);
  Clock clock_4 (.out(clock_4_out));
  mem_cell0 mem_cell0_25 (.\input (data_input), .mode(mode_input), .select(A0011_out), .\output (mem_cell0_25_output));
  mem_cell0 mem_cell0_26 (.\input (in_11), .mode(mode_input), .select(A0011_out), .\output (mem_cell0_26_output));
  mem_cell0 mem_cell0_27 (.\input (in_12), .mode(mode_input), .select(A0011_out), .\output (mem_cell0_27_output));
  mem_cell0 mem_cell0_28 (.\input (in_13), .mode(mode_input), .select(A0011_out), .\output (mem_cell0_28_output));
  mem_cell0 mem_cell0_29 (.\input (in_14), .mode(mode_input), .select(A0011_out), .\output (mem_cell0_29_output));
  mem_cell0 mem_cell0_30 (.\input (in_15), .mode(mode_input), .select(A0011_out), .\output (mem_cell0_30_output));
  mem_cell0 mem_cell0_31 (.\input (in_16), .mode(mode_input), .select(A0011_out), .\output (mem_cell0_31_output));
  mem_cell0 mem_cell0_32 (.\input (in_17), .mode(mode_input), .select(A0011_out), .\output (mem_cell0_32_output));
  and A0100 (A0100_out, address_input, in_4, in_5, in_7);
  or or_1 (or_1_out, mem_cell0_1_output, mem_cell0_9_output, mem_cell0_17_output, mem_cell0_25_output);
  or or_2 (or_2_out, mem_cell0_2_output, mem_cell0_10_output, mem_cell0_18_output, mem_cell0_26_output);
  or or_3 (or_3_out, mem_cell0_3_output, mem_cell0_11_output, mem_cell0_19_output, mem_cell0_27_output);
  or or_4 (or_4_out, mem_cell0_4_output, mem_cell0_12_output, mem_cell0_20_output, mem_cell0_28_output);
  or or_5 (or_5_out, mem_cell0_5_output, mem_cell0_13_output, mem_cell0_21_output, mem_cell0_29_output);
  or or_6 (or_6_out, mem_cell0_6_output, mem_cell0_14_output, mem_cell0_22_output, mem_cell0_30_output);
  or or_7 (or_7_out, mem_cell0_7_output, mem_cell0_15_output, mem_cell0_23_output, mem_cell0_31_output);
  or or_8 (or_8_out, mem_cell0_8_output, mem_cell0_16_output, mem_cell0_24_output, mem_cell0_32_output);
  Clock clock_5 (.out(clock_5_out));
  mem_cell0 mem_cell0_33 (.\input (data_input), .mode(mode_input), .select(A0100_out), .\output (mem_cell0_33_output));
  mem_cell0 mem_cell0_34 (.\input (in_11), .mode(mode_input), .select(A0100_out), .\output (mem_cell0_34_output));
  mem_cell0 mem_cell0_35 (.\input (in_12), .mode(mode_input), .select(A0100_out), .\output (mem_cell0_35_output));
  mem_cell0 mem_cell0_36 (.\input (in_13), .mode(mode_input), .select(A0100_out), .\output (mem_cell0_36_output));
  mem_cell0 mem_cell0_37 (.\input (in_14), .mode(mode_input), .select(A0100_out), .\output (mem_cell0_37_output));
  mem_cell0 mem_cell0_38 (.\input (in_15), .mode(mode_input), .select(A0100_out), .\output (mem_cell0_38_output));
  mem_cell0 mem_cell0_39 (.\input (in_16), .mode(mode_input), .select(A0100_out), .\output (mem_cell0_39_output));
  mem_cell0 mem_cell0_40 (.\input (in_17), .mode(mode_input), .select(A0100_out), .\output (mem_cell0_40_output));
  and A0101 (A0101_out, address_input, in_4, in_5, in_8);
  Clock clock_6 (.out(clock_6_out));
  mem_cell0 mem_cell0_41 (.\input (data_input), .mode(mode_input), .select(A0101_out), .\output (mem_cell0_41_output));
  mem_cell0 mem_cell0_42 (.\input (in_11), .mode(mode_input), .select(A0101_out), .\output (mem_cell0_42_output));
  mem_cell0 mem_cell0_43 (.\input (in_12), .mode(mode_input), .select(A0101_out), .\output (mem_cell0_43_output));
  mem_cell0 mem_cell0_44 (.\input (in_13), .mode(mode_input), .select(A0101_out), .\output (mem_cell0_44_output));
  mem_cell0 mem_cell0_45 (.\input (in_14), .mode(mode_input), .select(A0101_out), .\output (mem_cell0_45_output));
  mem_cell0 mem_cell0_46 (.\input (in_15), .mode(mode_input), .select(A0101_out), .\output (mem_cell0_46_output));
  mem_cell0 mem_cell0_47 (.\input (in_16), .mode(mode_input), .select(A0101_out), .\output (mem_cell0_47_output));
  mem_cell0 mem_cell0_48 (.\input (in_17), .mode(mode_input), .select(A0101_out), .\output (mem_cell0_48_output));
  and A0110 (A0110_out, address_input, in_4, in_6, in_7);
  Clock clock_7 (.out(clock_7_out));
  mem_cell0 mem_cell0_49 (.\input (data_input), .mode(mode_input), .select(A0110_out), .\output (mem_cell0_49_output));
  mem_cell0 mem_cell0_50 (.\input (in_11), .mode(mode_input), .select(A0110_out), .\output (mem_cell0_50_output));
  mem_cell0 mem_cell0_51 (.\input (in_12), .mode(mode_input), .select(A0110_out), .\output (mem_cell0_51_output));
  mem_cell0 mem_cell0_52 (.\input (in_13), .mode(mode_input), .select(A0110_out), .\output (mem_cell0_52_output));
  mem_cell0 mem_cell0_53 (.\input (in_14), .mode(mode_input), .select(A0110_out), .\output (mem_cell0_53_output));
  mem_cell0 mem_cell0_54 (.\input (in_15), .mode(mode_input), .select(A0110_out), .\output (mem_cell0_54_output));
  mem_cell0 mem_cell0_55 (.\input (in_16), .mode(mode_input), .select(A0110_out), .\output (mem_cell0_55_output));
  mem_cell0 mem_cell0_56 (.\input (in_17), .mode(mode_input), .select(A0110_out), .\output (mem_cell0_56_output));
  and A0111 (A0111_out, address_input, in_4, in_6, in_8);
  Clock clock_8 (.out(clock_8_out));
  mem_cell0 mem_cell0_57 (.\input (data_input), .mode(mode_input), .select(A0111_out), .\output (mem_cell0_57_output));
  mem_cell0 mem_cell0_58 (.\input (in_11), .mode(mode_input), .select(A0111_out), .\output (mem_cell0_58_output));
  mem_cell0 mem_cell0_59 (.\input (in_12), .mode(mode_input), .select(A0111_out), .\output (mem_cell0_59_output));
  mem_cell0 mem_cell0_60 (.\input (in_13), .mode(mode_input), .select(A0111_out), .\output (mem_cell0_60_output));
  mem_cell0 mem_cell0_61 (.\input (in_14), .mode(mode_input), .select(A0111_out), .\output (mem_cell0_61_output));
  mem_cell0 mem_cell0_62 (.\input (in_15), .mode(mode_input), .select(A0111_out), .\output (mem_cell0_62_output));
  mem_cell0 mem_cell0_63 (.\input (in_16), .mode(mode_input), .select(A0111_out), .\output (mem_cell0_63_output));
  mem_cell0 mem_cell0_64 (.\input (in_17), .mode(mode_input), .select(A0111_out), .\output (mem_cell0_64_output));
  or or_9 (or_9_out, mem_cell0_33_output, mem_cell0_41_output, or_1_out, mem_cell0_49_output, mem_cell0_57_output);
  or or_10 (or_10_out, mem_cell0_34_output, mem_cell0_42_output, or_2_out, mem_cell0_50_output, mem_cell0_58_output);
  or or_11 (or_11_out, mem_cell0_35_output, mem_cell0_43_output, or_3_out, mem_cell0_51_output, mem_cell0_59_output);
  or or_12 (or_12_out, mem_cell0_36_output, mem_cell0_44_output, or_4_out, mem_cell0_52_output, mem_cell0_60_output);
  or or_13 (or_13_out, mem_cell0_37_output, mem_cell0_45_output, or_5_out, mem_cell0_53_output, mem_cell0_61_output);
  or or_14 (or_14_out, mem_cell0_38_output, mem_cell0_46_output, or_6_out, mem_cell0_54_output, mem_cell0_62_output);
  or or_15 (or_15_out, mem_cell0_39_output, mem_cell0_47_output, or_7_out, mem_cell0_55_output, mem_cell0_63_output);
  or or_16 (or_16_out, mem_cell0_40_output, mem_cell0_48_output, or_8_out, mem_cell0_56_output, mem_cell0_64_output);
  and A1000 (A1000_out, in_2, in_3, in_5, in_7);
  Clock clock_9 (.out(clock_9_out));
  mem_cell0 mem_cell0_65 (.\input (data_input), .mode(mode_input), .select(A1000_out), .\output (mem_cell0_65_output));
  mem_cell0 mem_cell0_66 (.\input (in_11), .mode(mode_input), .select(A1000_out), .\output (mem_cell0_66_output));
  mem_cell0 mem_cell0_67 (.\input (in_12), .mode(mode_input), .select(A1000_out), .\output (mem_cell0_67_output));
  mem_cell0 mem_cell0_68 (.\input (in_13), .mode(mode_input), .select(A1000_out), .\output (mem_cell0_68_output));
  mem_cell0 mem_cell0_69 (.\input (in_14), .mode(mode_input), .select(A1000_out), .\output (mem_cell0_69_output));
  mem_cell0 mem_cell0_70 (.\input (in_15), .mode(mode_input), .select(A1000_out), .\output (mem_cell0_70_output));
  mem_cell0 mem_cell0_71 (.\input (in_16), .mode(mode_input), .select(A1000_out), .\output (mem_cell0_71_output));
  mem_cell0 mem_cell0_72 (.\input (in_17), .mode(mode_input), .select(A1000_out), .\output (mem_cell0_72_output));
  and A1001 (A1001_out, in_2, in_3, in_5, in_8);
  Clock clock_10 (.out(clock_10_out));
  mem_cell0 mem_cell0_73 (.\input (data_input), .mode(mode_input), .select(A1001_out), .\output (mem_cell0_73_output));
  mem_cell0 mem_cell0_74 (.\input (in_11), .mode(mode_input), .select(A1001_out), .\output (mem_cell0_74_output));
  mem_cell0 mem_cell0_75 (.\input (in_12), .mode(mode_input), .select(A1001_out), .\output (mem_cell0_75_output));
  mem_cell0 mem_cell0_76 (.\input (in_13), .mode(mode_input), .select(A1001_out), .\output (mem_cell0_76_output));
  mem_cell0 mem_cell0_77 (.\input (in_14), .mode(mode_input), .select(A1001_out), .\output (mem_cell0_77_output));
  mem_cell0 mem_cell0_78 (.\input (in_15), .mode(mode_input), .select(A1001_out), .\output (mem_cell0_78_output));
  mem_cell0 mem_cell0_79 (.\input (in_16), .mode(mode_input), .select(A1001_out), .\output (mem_cell0_79_output));
  mem_cell0 mem_cell0_80 (.\input (in_17), .mode(mode_input), .select(A1001_out), .\output (mem_cell0_80_output));
  and A1010 (A1010_out, in_2, in_3, in_6, in_7);
  Clock clock_11 (.out(clock_11_out));
  mem_cell0 mem_cell0_81 (.\input (data_input), .mode(mode_input), .select(A1010_out), .\output (mem_cell0_81_output));
  mem_cell0 mem_cell0_82 (.\input (in_11), .mode(mode_input), .select(A1010_out), .\output (mem_cell0_82_output));
  mem_cell0 mem_cell0_83 (.\input (in_12), .mode(mode_input), .select(A1010_out), .\output (mem_cell0_83_output));
  mem_cell0 mem_cell0_84 (.\input (in_13), .mode(mode_input), .select(A1010_out), .\output (mem_cell0_84_output));
  mem_cell0 mem_cell0_85 (.\input (in_14), .mode(mode_input), .select(A1010_out), .\output (mem_cell0_85_output));
  mem_cell0 mem_cell0_86 (.\input (in_15), .mode(mode_input), .select(A1010_out), .\output (mem_cell0_86_output));
  mem_cell0 mem_cell0_87 (.\input (in_16), .mode(mode_input), .select(A1010_out), .\output (mem_cell0_87_output));
  mem_cell0 mem_cell0_88 (.\input (in_17), .mode(mode_input), .select(A1010_out), .\output (mem_cell0_88_output));
  and A1011 (A1011_out, in_2, in_3, in_6, in_8);
  Clock clock_12 (.out(clock_12_out));
  mem_cell0 mem_cell0_89 (.\input (data_input), .mode(mode_input), .select(A1011_out), .\output (mem_cell0_89_output));
  mem_cell0 mem_cell0_90 (.\input (in_11), .mode(mode_input), .select(A1011_out), .\output (mem_cell0_90_output));
  mem_cell0 mem_cell0_91 (.\input (in_12), .mode(mode_input), .select(A1011_out), .\output (mem_cell0_91_output));
  mem_cell0 mem_cell0_92 (.\input (in_13), .mode(mode_input), .select(A1011_out), .\output (mem_cell0_92_output));
  mem_cell0 mem_cell0_93 (.\input (in_14), .mode(mode_input), .select(A1011_out), .\output (mem_cell0_93_output));
  mem_cell0 mem_cell0_94 (.\input (in_15), .mode(mode_input), .select(A1011_out), .\output (mem_cell0_94_output));
  mem_cell0 mem_cell0_95 (.\input (in_16), .mode(mode_input), .select(A1011_out), .\output (mem_cell0_95_output));
  mem_cell0 mem_cell0_96 (.\input (in_17), .mode(mode_input), .select(A1011_out), .\output (mem_cell0_96_output));
  and A1100 (A1100_out, in_2, in_4, in_5, in_7);
  or or_17 (or_17_out, mem_cell0_65_output, mem_cell0_73_output, or_9_out, mem_cell0_81_output, mem_cell0_89_output);
  or or_18 (or_18_out, mem_cell0_66_output, mem_cell0_74_output, or_10_out, mem_cell0_82_output, mem_cell0_90_output);
  or or_19 (or_19_out, mem_cell0_67_output, mem_cell0_75_output, or_11_out, mem_cell0_83_output, mem_cell0_91_output);
  or or_20 (or_20_out, mem_cell0_68_output, mem_cell0_76_output, or_12_out, mem_cell0_84_output, mem_cell0_92_output);
  or or_21 (or_21_out, mem_cell0_69_output, mem_cell0_77_output, or_13_out, mem_cell0_85_output, mem_cell0_93_output);
  or or_22 (or_22_out, mem_cell0_70_output, mem_cell0_78_output, or_14_out, mem_cell0_86_output, mem_cell0_94_output);
  or or_23 (or_23_out, mem_cell0_71_output, mem_cell0_79_output, or_15_out, mem_cell0_87_output, mem_cell0_95_output);
  or or_24 (or_24_out, mem_cell0_72_output, mem_cell0_80_output, or_16_out, mem_cell0_88_output, mem_cell0_96_output);
  Clock clock_13 (.out(clock_13_out));
  mem_cell0 mem_cell0_97 (.\input (data_input), .mode(mode_input), .select(A1100_out), .\output (mem_cell0_97_output));
  mem_cell0 mem_cell0_98 (.\input (in_11), .mode(mode_input), .select(A1100_out), .\output (mem_cell0_98_output));
  mem_cell0 mem_cell0_99 (.\input (in_12), .mode(mode_input), .select(A1100_out), .\output (mem_cell0_99_output));
  mem_cell0 mem_cell0_100 (.\input (in_13), .mode(mode_input), .select(A1100_out), .\output (mem_cell0_100_output));
  mem_cell0 mem_cell0_101 (.\input (in_14), .mode(mode_input), .select(A1100_out), .\output (mem_cell0_101_output));
  mem_cell0 mem_cell0_102 (.\input (in_15), .mode(mode_input), .select(A1100_out), .\output (mem_cell0_102_output));
  mem_cell0 mem_cell0_103 (.\input (in_16), .mode(mode_input), .select(A1100_out), .\output (mem_cell0_103_output));
  mem_cell0 mem_cell0_104 (.\input (in_17), .mode(mode_input), .select(A1100_out), .\output (mem_cell0_104_output));
  and A1101 (A1101_out, in_2, in_4, in_5, in_8);
  Clock clock_14 (.out(clock_14_out));
  mem_cell0 mem_cell0_105 (
    .\input (data_input), .mode(mode_input), .select(A1101_out), .\output (mem_cell0_105_output));
  mem_cell0 mem_cell0_106 (.\input (in_11), .mode(mode_input), .select(A1101_out), .\output (mem_cell0_106_output));
  mem_cell0 mem_cell0_107 (.\input (in_12), .mode(mode_input), .select(A1101_out), .\output (mem_cell0_107_output));
  mem_cell0 mem_cell0_108 (.\input (in_13), .mode(mode_input), .select(A1101_out), .\output (mem_cell0_108_output));
  mem_cell0 mem_cell0_109 (.\input (in_14), .mode(mode_input), .select(A1101_out), .\output (mem_cell0_109_output));
  mem_cell0 mem_cell0_110 (.\input (in_15), .mode(mode_input), .select(A1101_out), .\output (mem_cell0_110_output));
  mem_cell0 mem_cell0_111 (.\input (in_16), .mode(mode_input), .select(A1101_out), .\output (mem_cell0_111_output));
  mem_cell0 mem_cell0_112 (.\input (in_17), .mode(mode_input), .select(A1101_out), .\output (mem_cell0_112_output));
  and A1110 (A1110_out, in_2, in_4, in_6, in_7);
  Clock clock_15 (.out(clock_15_out));
  mem_cell0 mem_cell0_113 (
    .\input (data_input), .mode(mode_input), .select(A1110_out), .\output (mem_cell0_113_output));
  mem_cell0 mem_cell0_114 (.\input (in_11), .mode(mode_input), .select(A1110_out), .\output (mem_cell0_114_output));
  mem_cell0 mem_cell0_115 (.\input (in_12), .mode(mode_input), .select(A1110_out), .\output (mem_cell0_115_output));
  mem_cell0 mem_cell0_116 (.\input (in_13), .mode(mode_input), .select(A1110_out), .\output (mem_cell0_116_output));
  mem_cell0 mem_cell0_117 (.\input (in_14), .mode(mode_input), .select(A1110_out), .\output (mem_cell0_117_output));
  mem_cell0 mem_cell0_118 (.\input (in_15), .mode(mode_input), .select(A1110_out), .\output (mem_cell0_118_output));
  mem_cell0 mem_cell0_119 (.\input (in_16), .mode(mode_input), .select(A1110_out), .\output (mem_cell0_119_output));
  mem_cell0 mem_cell0_120 (.\input (in_17), .mode(mode_input), .select(A1110_out), .\output (mem_cell0_120_output));
  and A111 (A111_out, in_2, in_4, in_6, in_8);
  Clock clock_16 (.out(clock_16_out));
  mem_cell0 mem_cell0_121 (.\input (data_input), .mode(mode_input), .select(A111_out), .\output (mem_cell0_121_output));
  mem_cell0 mem_cell0_122 (.\input (in_11), .mode(mode_input), .select(A111_out), .\output (mem_cell0_122_output));
  mem_cell0 mem_cell0_123 (.\input (in_12), .mode(mode_input), .select(A111_out), .\output (mem_cell0_123_output));
  mem_cell0 mem_cell0_124 (.\input (in_13), .mode(mode_input), .select(A111_out), .\output (mem_cell0_124_output));
  mem_cell0 mem_cell0_125 (.\input (in_14), .mode(mode_input), .select(A111_out), .\output (mem_cell0_125_output));
  mem_cell0 mem_cell0_126 (.\input (in_15), .mode(mode_input), .select(A111_out), .\output (mem_cell0_126_output));
  mem_cell0 mem_cell0_127 (.\input (in_16), .mode(mode_input), .select(A111_out), .\output (mem_cell0_127_output));
  mem_cell0 mem_cell0_128 (.\input (in_17), .mode(mode_input), .select(A111_out), .\output (mem_cell0_128_output));
  or or_25 (or_25_out, mem_cell0_97_output, mem_cell0_105_output, or_17_out, mem_cell0_113_output, mem_cell0_121_output);
  or or_26 (or_26_out, mem_cell0_98_output, mem_cell0_106_output, or_18_out, mem_cell0_114_output, mem_cell0_122_output);
  or or_27 (or_27_out, mem_cell0_99_output, mem_cell0_107_output, or_19_out, mem_cell0_115_output, mem_cell0_123_output);
  or or_28 (or_28_out, mem_cell0_100_output, mem_cell0_108_output, or_20_out, mem_cell0_116_output, mem_cell0_124_output);
  or or_29 (or_29_out, mem_cell0_101_output, mem_cell0_109_output, or_21_out, mem_cell0_117_output, mem_cell0_125_output);
  or or_30 (or_30_out, mem_cell0_102_output, mem_cell0_110_output, or_22_out, mem_cell0_118_output, mem_cell0_126_output);
  or or_31 (or_31_out, mem_cell0_103_output, mem_cell0_111_output, or_23_out, mem_cell0_119_output, mem_cell0_127_output);
  or or_32 (or_32_out, mem_cell0_104_output, mem_cell0_112_output, or_24_out, mem_cell0_120_output, mem_cell0_128_output);

  // Notes on the sheet:
  //   data space
  //   address space
  //   RAM
  //   data output
endmodule

module ADDR_REG (
  input  in_1,
  input  in_2,
  input  in_3,
  input  in_4,
  input  in_5,
  output out_6,
  output out_7,
  output out_8,
  output out_9,
  output out_10,
  output out_11,
  output out_12,
  output out_13
);

  D_Flip_Flop d_ff_1 (.D(in_1), .clk(in_5), .Q(out_7));  // open: Qn, preset, reset
  D_Flip_Flop d_ff_2 (.D(in_2), .clk(in_5), .Q(out_9));  // open: Qn, preset, reset
  D_Flip_Flop d_ff_3 (.D(in_3), .clk(in_5), .Q(out_11));  // open: Qn, preset, reset
  D_Flip_Flop d_ff_4 (.D(in_4), .clk(in_5), .Q(out_13));  // open: Qn, preset, reset
  not not_1 (out_6, out_7);
  not not_2 (out_8, out_9);
  not not_3 (out_10, out_11);
  not not_4 (out_12, out_13);

  // Notes on the sheet:
  //   ADDRESS REGISTER
  //   addr input
endmodule

module DATA_REG (
  input  mode_input,
  input  in_2,
  input  in_3,
  input  in_4,
  input  in_5,
  input  data_input,
  input  in_7,
  input  in_8,
  input  in_9,
  output out_10,
  output out_11,
  output out_12,
  output out_13,
  output out_14,
  output out_15,
  output out_16,
  output out_17
);

  wire and_1_out, and_2_out, and_3_out, and_4_out, and_5_out, and_6_out, and_7_out, and_8_out, clock_1_out,
       clock_2_out, d_ff_1_q, d_ff_2_q, d_ff_3_q, d_ff_4_q, d_ff_5_q, d_ff_6_q, d_ff_7_q, d_ff_8_q,
       not_1_out, not_2_out, not_3_out, not_4_out, not_5_out, not_6_out, not_7_out, not_8_out, undriven,
       undriven_2, undriven_3, undriven_4, undriven_5, undriven_6, undriven_7, undriven_8;

  and and_1 (and_1_out, mode_input, in_2);
  Clock clock_1 (.out(clock_1_out));
  and and_2 (and_2_out, in_3, mode_input);
  and and_3 (and_3_out, mode_input, in_4);
  and and_4 (and_4_out, in_5, mode_input);
  and and_5 (and_5_out, mode_input, data_input);
  Clock clock_2 (.out(clock_2_out));
  and and_6 (and_6_out, in_7, mode_input);
  and and_7 (and_7_out, mode_input, in_8);
  and and_8 (and_8_out, in_9, mode_input);
  D_Flip_Flop d_ff_1 (.D(and_1_out), .clk(clock_1_out), .Q(d_ff_1_q));  // open: Qn, preset, reset
  D_Flip_Flop d_ff_2 (.D(and_2_out), .clk(clock_1_out), .Q(d_ff_2_q));  // open: Qn, preset, reset
  D_Flip_Flop d_ff_3 (.D(and_3_out), .clk(clock_1_out), .Q(d_ff_3_q));  // open: Qn, preset, reset
  D_Flip_Flop d_ff_4 (.D(and_4_out), .clk(clock_1_out), .Q(d_ff_4_q));  // open: Qn, preset, reset
  D_Flip_Flop d_ff_5 (.D(and_5_out), .clk(clock_2_out), .Q(d_ff_5_q));  // open: Qn, preset, reset
  D_Flip_Flop d_ff_6 (.D(and_6_out), .clk(clock_2_out), .Q(d_ff_6_q));  // open: Qn, preset, reset
  D_Flip_Flop d_ff_7 (.D(and_7_out), .clk(clock_2_out), .Q(d_ff_7_q));  // open: Qn, preset, reset
  D_Flip_Flop d_ff_8 (.D(and_8_out), .clk(clock_2_out), .Q(d_ff_8_q));  // open: Qn, preset, reset
  not not_1 (not_1_out, mode_input);
  not not_2 (not_2_out, mode_input);
  not not_3 (not_3_out, mode_input);
  not not_4 (not_4_out, mode_input);
  not not_5 (not_5_out, mode_input);
  not not_6 (not_6_out, mode_input);
  not not_7 (not_7_out, mode_input);
  not not_8 (not_8_out, mode_input);
  and and_9 (out_10, undriven, not_1_out);
  and and_10 (out_11, undriven_2, not_2_out);
  and and_11 (out_12, undriven_3, not_3_out);
  and and_12 (out_13, undriven_4, not_4_out);
  and and_13 (out_14, undriven_5, not_5_out);
  and and_14 (out_15, undriven_6, not_6_out);
  and and_15 (out_16, undriven_7, not_7_out);
  and and_16 (out_17, undriven_8, not_8_out);

  // Notes on the sheet:
  //   DATA REGISTER
  //   clk
  //   clk
  //   data output
endmodule

module MODE_REG (
  input  \input ,
  input  in_2,
  output \output 
);

  wire not_1_out;

  J_K_Flip_Flop j_k_ff_1 (.J(\input ), .K(not_1_out), .clk(in_2), .Q(\output ));  // open: Qn, preset, reset
  not not_1 (not_1_out, \input );
endmodule

module roughmainCPU (
  input  in_1,
  input  in_2,
  input  in_3,
  input  in_4,
  input  in_5,
  input  in_6,
  input  in_7,
  input  in_8,
  input  in_9,
  input  in_10,
  input  in_11,
  input  in_12,
  input  in_13,
  output out_14,
  output out_15,
  output out_16,
  output out_17,
  output out_18,
  output out_19,
  output out_20,
  output out_21
);

  wire addr_reg_1_out_6, addr_reg_1_out_7, addr_reg_1_out_8, addr_reg_1_out_9, addr_reg_1_out_10,
       addr_reg_1_out_11, addr_reg_1_out_12, addr_reg_1_out_13, clock_1_out, mode_reg_1_output;

  Clock clock_1 (.out(clock_1_out));
  ADDR_REG addr_reg_1 (
    .out_10(addr_reg_1_out_10), .out_9(addr_reg_1_out_9), .out_8(addr_reg_1_out_8), .out_7(addr_reg_1_out_7),
    .out_6(addr_reg_1_out_6), .in_5(clock_1_out), .in_4(in_4), .in_3(in_3), .in_2(in_2), .in_1(in_1),
    .out_11(addr_reg_1_out_11), .out_12(addr_reg_1_out_12), .out_13(addr_reg_1_out_13));
  MODE_REG mode_reg_1 (.\output (mode_reg_1_output), .in_2(clock_1_out), .\input (in_6));
  RAM_16bytes ram_16bytes_1 (
    .out_18(out_14), .in_14(in_10), .in_17(in_13), .in_15(in_11), .in_16(in_12), .in_13(in_9), .in_12(in_8),
    .in_11(in_7), .data_input(in_5), .mode_input(mode_reg_1_output), .in_8(addr_reg_1_out_13),
    .in_7(addr_reg_1_out_12), .in_6(addr_reg_1_out_11), .in_5(addr_reg_1_out_10), .in_4(addr_reg_1_out_9),
    .in_3(addr_reg_1_out_8), .in_2(addr_reg_1_out_7), .address_input(addr_reg_1_out_6), .out_19(out_15),
    .out_20(out_16), .out_21(out_17), .out_22(out_18), .out_23(out_19), .out_24(out_20), .out_25(out_21));
endmodule
